// Logisim project alu.circ as structural Verilog: 2 circuits, main circuit main
module main (
  input  [15:0] X,
  input  [15:0] Y,
  input  [3:0] Switch__S,
  output Signed_Overflow,
  output [15:0] RESULT,
  output Equal
);

  all_ops all_ops_1 (.X(X), .Y(Y), .Switch__S(Switch__S), .overflow(Signed_Overflow), .out(RESULT));
  Comparator #(.width(16)) comparator_1 (.a(X), .b(Y), .eq(Equal));  // open: gt, lt

  // Notes on the sheet:
  //   INPUTS to your circuit
  //   INPUT to your circuit
  //   DON'T CHANGE THE INPUTS AND OUTPUTS! IF YOU DO SO, YOU NEED TO MAKE SURE THE PINS ARE IN THE RIGHT PLACES!
  //   OUTPUTS of your circuit
endmodule

module all_ops (
  input  [15:0] X,
  input  [15:0] Y,
  input  [3:0] Switch__S,
  output overflow,
  output [15:0] out
);

  wire comparator_1_lt, o1, o2, o3, o4;
  wire [15:0] add, addp8, \and , lui, \or , sllv, slt, srav, srlv, sub;

  Adder #(.width(16)) adder_1 (.a(X), .b(Y), .out(add), .cout(o1));  // open: cin
  Shifter #(.width(16), .shift("lr")) shifter_1 (.in(X), .\dist (Y[3:0]), .out(srlv));
  Comparator #(.width(16)) comparator_1 (.a(X), .b(Y), .lt(comparator_1_lt));  // open: gt, eq
  assign \and  = X & Y;  // AND_Gate and_1, 16 bits wide
  Adder adder_2 (.a(X[7:0]), .b(Y[7:0]), .out(addp8[7:0]), .cout(o3));  // open: cin
  Adder adder_3 (.a(X[15:8]), .b(Y[15:8]), .out(addp8[15:8]));  // open: cin, cout
  Shifter #(.width(16)) shifter_2 (.in(Y), .\dist (4'b1000), .out(lui));
  assign slt = {{15{1'b0}}, comparator_1_lt};  // Bit_Extender bit_extender_1
  Subtractor #(.width(16)) subtractor_1 (.a(X), .b(Y), .out(sub), .bout(o2));  // open: bin
  Shifter #(.width(16), .shift("ar")) shifter_3 (.in(X), .\dist (Y[3:0]), .out(srav));
  assign \or  = X | Y;  // OR_Gate or_1, 16 bits wide
  Subtractor subtractor_2 (.a(X[7:0]), .b(Y[7:0]), .out(addp8[7:0]), .bout(o4));  // open: bin
  Subtractor subtractor_3 (.a(X[15:8]), .b(Y[15:8]), .out(addp8[15:8]));  // open: bin, bout
  Shifter #(.width(16)) shifter_4 (.in(X), .\dist (Y[3:0]), .out(sllv));
  Multiplexer #(.select(4), .width(16)) multiplexer_1 (
    .in0(add), .in1(sub), .in2(sllv), .in3(srlv), .in4(srav), .in5(slt), .in6(\or ), .in7(\and ),
    .in8(addp8), .in9(addp8), .in10(lui), .out(out), .sel(Switch__S));  // open: in11, in12, in13, in14, in15, en
  Multiplexer #(.select(4)) multiplexer_2 (
    .in0(o1), .in1(o2), .in2(1'b0), .in3(1'b0), .in4(1'b0), .in5(1'b0), .in6(1'b0), .in7(1'b0), .in8(o3),
    .in9(o4), .out(overflow), .sel(Switch__S));  // open: in10, in11, in12, in13, in14, in15, en

  // Other names for the same wires on the sheet: switch[3:0] = Switch__S; _07x[7:0] = X[7:0]; _815x[7:0] = X[15:8];
  //   _07y[7:0] = Y[7:0]; _815y[7:0] = Y[15:8]
endmodule
