// Logisim project cpu.circ as structural Verilog: 2 circuits, main circuit main
module main (
  input  [15:0] From_Instr_Mem,
  input  clk,
  output [15:0] r0,
  output [15:0] r1,
  output [15:0] r2,
  output [15:0] r3,
  output [15:0] Display_0,
  output [15:0] Display_1,
  output [15:0] To_Instr_Mem,
  output [15:0] Data_Mem_Data,
  output [15:0] Data_Mem_Addr,
  output Data_Mem_Write
);

  wire ALUSrc, button_1_out, equal, ExtOp, MemtoReg, overflow, RegDst, RegWr;
  wire [1:0] nPC_sel, wr_reg;
  wire [3:0] ALUctr;
  wire [15:0] adder_1_out, adder_2_out, and_1_out, bit_extender_1_out, bit_extender_2_out,
       bit_extender_3_out, bit_extender_4_out, ext_imm, mem_res, multiplexer_1_out, or_1_out, rs_val, wr_dat;

  control control_1 (
    .instruction(From_Instr_Mem), .Equal(equal), .nPC_sel(nPC_sel), .RegDst(RegDst), .ExtOp(ExtOp),
    .RegWr(RegWr), .ALUSrc(ALUSrc), .ALUctr(ALUctr), .MemtoReg(MemtoReg), .MemWr(Data_Mem_Write));
  Multiplexer #(.width(16)) multiplexer_1 (
    .in0(ext_imm), .in1(Data_Mem_Data), .out(multiplexer_1_out), .sel(ALUSrc));  // open: en
  Regfile_main Regfile (
    .Read_register_1(From_Instr_Mem[11:10]), .Read_register_2(From_Instr_Mem[9:8]), .write_register(wr_reg),
    .write_data(wr_dat), .Reg_0_Value(r0), .Reg_1_Value(r1), .Reg_2_Value(r2), .Reg_3_Value(r3),
    .RegWrite(RegWr), .clock(clk), .Read_Data_1(rs_val), .Read_Data_2(Data_Mem_Data));
  alu_main ALU (
    .Switch__S(ALUctr), .X(rs_val), .Equal(equal), .RESULT(Data_Mem_Addr), .Signed_Overflow(overflow),
    .Y(multiplexer_1_out));
  Multiplexer #(.width(16)) multiplexer_2 (
    .in0(Data_Mem_Addr), .in1(mem_res), .out(wr_dat), .sel(MemtoReg));  // open: en
  assign bit_extender_1_out = {{4{1'b0}}, From_Instr_Mem[11:0]};  // Bit_Extender bit_extender_1
  Button button_1 (.out(button_1_out));
  assign bit_extender_2_out = {{8{From_Instr_Mem[7]}}, From_Instr_Mem[7:0]};  // Bit_Extender bit_extender_2
  assign and_1_out = From_Instr_Mem & 16'hf000;  // AND_Gate and_1, 16 bits wide
  assign mem_res = Data_Mem_Write ? Data_Mem_Data : 16'bz;  // Controlled_Buffer controlled_buffer_1
  RAM #(.addrWidth(16), .dataWidth(16)) ram_1 (
    .addr(Data_Mem_Addr), .data(mem_res), .sel(1'b1), .clk(clk), .ld(Data_Mem_Write), .clr(button_1_out));
  Multiplexer #(.width(2)) multiplexer_3 (
    .in0(From_Instr_Mem[9:8]), .in1(From_Instr_Mem[7:6]), .out(wr_reg), .sel(RegDst));  // open: en
  assign bit_extender_3_out = {{8{1'b0}}, From_Instr_Mem[7:0]};  // Bit_Extender bit_extender_3
  assign bit_extender_4_out = {{8{From_Instr_Mem[7]}}, From_Instr_Mem[7:0]};  // Bit_Extender bit_extender_4
  Adder #(.width(16)) adder_1 (.a(From_Instr_Mem), .b(16'h1), .out(adder_1_out));  // open: cin, cout
  Adder #(.width(16)) adder_2 (.a(From_Instr_Mem), .b(bit_extender_2_out), .out(adder_2_out));  // open: cin, cout
  assign or_1_out = and_1_out | bit_extender_1_out;  // OR_Gate or_1, 16 bits wide
  Multiplexer #(.width(16)) multiplexer_4 (
    .in0(bit_extender_3_out), .in1(bit_extender_4_out), .out(ext_imm), .sel(ExtOp));  // open: en
  Multiplexer #(.select(2), .width(16)) multiplexer_5 (
    .in0(adder_1_out), .in1(adder_2_out), .in2(or_1_out), .out(To_Instr_Mem), .sel(nPC_sel));  // open: in3, en

  // Other names for the same wires on the sheet: alu_res[15:0] = Data_Mem_Addr; d0[15:0] = Display_0;
  //   d1[15:0] = Display_1; imm[7:0] = From_Instr_Mem[7:0]; instr_in[15:0] = From_Instr_Mem;
  //   tar_addr[11:0] = From_Instr_Mem[11:0]; rd[1:0] = From_Instr_Mem[7:6]; rt[1:0] = From_Instr_Mem[9:8];
  //   rs[1:0] = From_Instr_Mem[11:10]; MemWr = Data_Mem_Write; next_instr[15:0] = To_Instr_Mem;
  //   rt_val[15:0] = Data_Mem_Data

  // Notes on the sheet:
  //   This is the current PC that you need to send as OUTPUT
  //   This is the instruction that you would receive as INPUT
  //   This is a CLK that is an INPUT driven from the harness.
  //   Remember, this circuit is loaded from the harness to be tested!
  //   DO NOT CHANGE THE LOCATIONS OF THE INPUTS OR OUTPUTS! IF YOU DO SO, YOU NEED TO MAKE SURE THE PINS ARE IN THE RIGHT PLACES!
  //   These are OUTPUTS of the circuit
  //   These are OUTPUTS of the circuit
endmodule

module control (
  input  [15:0] instruction,
  input  Equal,
  output [1:0] nPC_sel,
  output RegDst,
  output ExtOp,
  output RegWr,
  output ALUSrc,
  output [3:0] ALUctr,
  output MemtoReg,
  output MemWr
);

  wire not_1_out;
  wire [1:0] eq, neq;
  wire [3:0] aluop;

  assign eq = {{1{1'b0}}, Equal};  // Bit_Extender bit_extender_1
  not not_1 (not_1_out, Equal);
  assign neq = {{1{1'b0}}, not_1_out};  // Bit_Extender bit_extender_2
  Multiplexer #(.select(4), .enable("false")) multiplexer_1 (
    .in0(1'b0), .in1(1'b0), .in2(1'b0), .in3(1'b0), .in4(1'b0), .in5(1'b0), .in6(1'b0), .in7(1'b0),
    .in8(1'b0), .in9(1'b1), .in10(1'b0), .in11(1'b1), .in12(1'b0), .out(MemtoReg), .sel(instruction[15:12]));  // open: in13, in14, in15
  Multiplexer #(.select(4), .enable("false")) multiplexer_2 (
    .in0(1'b0), .in1(1'b0), .in2(1'b0), .in3(1'b0), .in4(1'b0), .in5(1'b0), .in6(1'b0), .in7(1'b0),
    .in8(1'b0), .in9(1'b1), .in10(1'b0), .in11(1'b0), .in12(1'b0), .out(MemWr), .sel(instruction[15:12]));  // open: in13, in14, in15
  Comparator #(.width(4)) comparator_1 (.a(instruction[15:12]), .b(4'b0000), .eq(RegDst));  // open: gt, lt
  Multiplexer #(.select(4), .enable("false")) multiplexer_3 (
    .in0(1'b0), .in1(1'b0), .in2(1'b0), .in3(1'b0), .in4(1'b1), .in5(1'b1), .in6(1'b0), .in7(1'b0),
    .in8(1'b1), .in9(1'b1), .in10(1'b0), .in11(1'b1), .in12(1'b0), .out(ExtOp), .sel(instruction[15:12]));  // open: in13, in14, in15
  Multiplexer #(.select(4), .enable("false")) multiplexer_4 (
    .in0(1'b0), .in1(1'b0), .in2(1'b0), .in3(1'b0), .in4(1'b1), .in5(1'b1), .in6(1'b1), .in7(1'b1),
    .in8(1'b1), .in9(1'b1), .in10(1'b1), .in11(1'b1), .in12(1'b1), .out(ALUSrc), .sel(instruction[15:12]));  // open: in13, in14, in15
  Multiplexer #(.width(4), .enable("false")) multiplexer_5 (
    .in0(aluop), .in1(instruction[3:0]), .sel(RegDst));  // open: out
  Multiplexer #(.select(4), .enable("false")) multiplexer_6 (
    .in0(1'b1), .in1(1'b1), .in2(1'b0), .in3(1'b0), .in4(1'b0), .in5(1'b1), .in6(1'b1), .in7(1'b1),
    .in8(1'b0), .in9(1'b0), .in10(1'b1), .in11(1'b1), .in12(1'b0), .out(RegWr), .sel(instruction[15:12]));  // open: in13, in14, in15
  Multiplexer #(.select(4), .width(4), .enable("false")) multiplexer_7 (
    .in0(instruction[3:0]), .in1(4'b1111), .in2(4'b1111), .in3(4'b1111), .in4(4'b1111), .in5(4'b0000),
    .in6(4'b0111), .in7(4'b0110), .in8(4'b1111), .in9(4'b0000), .in10(4'b0010), .in11(4'b0000),
    .in12(4'b1111), .out(ALUctr), .sel(instruction[15:12]));  // open: in13, in14, in15
  Multiplexer #(.select(4), .width(2), .enable("false")) multiplexer_8 (
    .in0(2'b00), .in1(2'b10), .in2(2'b10), .in3(2'b10), .in4(eq), .in5(2'b00), .in6(2'b00), .in7(2'b00),
    .in8(neq), .in9(2'b00), .in10(2'b00), .in11(2'b00), .in12(2'b00), .out(nPC_sel), .sel(instruction[15:12]));  // open: in13, in14, in15

  // Other names for the same wires on the sheet: ac[3:0] = ALUctr; as = ALUSrc; eo = ExtOp;
  //   func[5:0] = instruction[5:0]; op[3:0] = instruction[15:12]; isR = RegDst; mtr = MemtoReg; mw = MemWr;
  //   nps[1:0] = nPC_sel; rw = RegWr

  // Notes on the sheet:
  //   Determine MemtoReg
  //   Determine MemWr
  //   Determine ExtOp
  //   Determine ALUSrc
  //   Determine RegWr
  //   Determine ALUctr
  //   Determine ALUctr
  //   00 if PC+4, 01 if branch, 10 if jump
  //   Low if rt, high if rd
  //   Low if zero, high if sign
  //   High if register, low if immediate
  //   High if memory, low if alu
endmodule
